// Logisim project LogisimDesign.circ as structural Verilog
module RegisterFile (
  input  RegWrite,
  input  [3:0] rs,
  input  [3:0] rd,
  input  [3:0] rt,
  input  [15:0] WreiteData,
  output [15:0] data1,
  output [15:0] data2
);

  wire and_1_out, and_2_out, and_3_out, and_4_out, and_5_out, and_6_out, and_7_out, and_8_out, and_9_out,
       and_10_out, and_11_out, and_12_out, and_13_out, and_14_out, and_15_out, and_16_out, clock_1_out,
       decoder_1_out0, decoder_1_out1, decoder_1_out2, decoder_1_out3, decoder_1_out4, decoder_1_out5,
       decoder_1_out6, decoder_1_out7, decoder_1_out8, decoder_1_out9, decoder_1_out10, decoder_1_out11,
       decoder_1_out12, decoder_1_out13, decoder_1_out14, decoder_1_out15;
  wire [15:0] r0, r1, r2, r3, r4, r5, r6, r7, r8, r9, r10, r11, r12, r13, r14, r15;

  Decoder #(.select(4), .enable("false")) decoder_1 (
    .out0(decoder_1_out0), .out1(decoder_1_out1), .out2(decoder_1_out2), .out3(decoder_1_out3),
    .out4(decoder_1_out4), .out5(decoder_1_out5), .out6(decoder_1_out6), .out7(decoder_1_out7),
    .out8(decoder_1_out8), .out9(decoder_1_out9), .out10(decoder_1_out10), .out11(decoder_1_out11),
    .out12(decoder_1_out12), .out13(decoder_1_out13), .out14(decoder_1_out14), .out15(decoder_1_out15),
    .sel(rd));
  and and_1 (and_1_out, decoder_1_out0, RegWrite);
  and and_2 (and_2_out, decoder_1_out1, RegWrite);
  and and_3 (and_3_out, decoder_1_out2, RegWrite);
  and and_4 (and_4_out, decoder_1_out3, RegWrite);
  and and_5 (and_5_out, decoder_1_out4, RegWrite);
  and and_6 (and_6_out, decoder_1_out5, RegWrite);
  and and_7 (and_7_out, decoder_1_out6, RegWrite);
  and and_8 (and_8_out, decoder_1_out7, RegWrite);
  Register #(.width(16)) register_1 (.D(WreiteData), .en(and_1_out), .Q(r0), .clk(clock_1_out));  // open: clr
  Register #(.width(16)) register_2 (.D(WreiteData), .en(and_2_out), .Q(r1), .clk(clock_1_out));  // open: clr
  Register #(.width(16)) register_3 (.D(WreiteData), .en(and_3_out), .Q(r2), .clk(clock_1_out));  // open: clr
  Register #(.width(16)) register_4 (.D(WreiteData), .en(and_4_out), .Q(r3), .clk(clock_1_out));  // open: clr
  Register #(.width(16)) register_5 (.D(WreiteData), .en(and_5_out), .Q(r4), .clk(clock_1_out));  // open: clr
  Register #(.width(16)) register_6 (.D(WreiteData), .en(and_6_out), .Q(r5), .clk(clock_1_out));  // open: clr
  Register #(.width(16)) register_7 (.D(WreiteData), .en(and_7_out), .Q(r6), .clk(clock_1_out));  // open: clr
  Register #(.width(16)) register_8 (.D(WreiteData), .en(and_8_out), .Q(r7), .clk(clock_1_out));  // open: clr
  Clock clock_1 (.out(clock_1_out));
  and and_9 (and_9_out, decoder_1_out8, RegWrite);
  and and_10 (and_10_out, decoder_1_out9, RegWrite);
  and and_11 (and_11_out, decoder_1_out10, RegWrite);
  and and_12 (and_12_out, decoder_1_out11, RegWrite);
  and and_13 (and_13_out, decoder_1_out12, RegWrite);
  and and_14 (and_14_out, decoder_1_out13, RegWrite);
  and and_15 (and_15_out, decoder_1_out14, RegWrite);
  and and_16 (and_16_out, decoder_1_out15, RegWrite);
  Register #(.width(16)) register_9 (.D(WreiteData), .en(and_9_out), .Q(r8), .clk(clock_1_out));  // open: clr
  Register #(.width(16)) register_10 (.D(WreiteData), .en(and_10_out), .Q(r9), .clk(clock_1_out));  // open: clr
  Register #(.width(16)) register_11 (.D(WreiteData), .en(and_11_out), .Q(r10), .clk(clock_1_out));  // open: clr
  Register #(.width(16)) register_12 (.D(WreiteData), .en(and_12_out), .Q(r11), .clk(clock_1_out));  // open: clr
  Register #(.width(16)) register_13 (.D(WreiteData), .en(and_13_out), .Q(r12), .clk(clock_1_out));  // open: clr
  Register #(.width(16)) register_14 (.D(WreiteData), .en(and_14_out), .Q(r13), .clk(clock_1_out));  // open: clr
  Register #(.width(16)) register_15 (.D(WreiteData), .en(and_15_out), .Q(r14), .clk(clock_1_out));  // open: clr
  Register #(.width(16)) register_16 (.D(WreiteData), .en(and_16_out), .Q(r15), .clk(clock_1_out));  // open: clr
  Multiplexer #(.select(4), .width(16), .enable("false")) multiplexer_1 (
    .in0(r0), .in1(r1), .in2(r2), .in3(r3), .in4(r4), .in5(r5), .in6(r6), .in7(r7), .in8(r8), .in9(r9),
    .in10(r10), .in11(r11), .in12(r12), .in13(r13), .in14(r14), .in15(r15), .out(data1), .sel(rs));
  Multiplexer #(.select(4), .width(16), .enable("false")) multiplexer_2 (
    .in0(r0), .in1(r1), .in2(r2), .in3(r3), .in4(r4), .in5(r5), .in6(r6), .in7(r7), .in8(r8), .in9(r9),
    .in10(r10), .in11(r11), .in12(r12), .in13(r13), .in14(r14), .in15(r15), .out(data2), .sel(rt));
endmodule

module ControlUnit (
  input  [3:0] opcode,
  input  [3:0] funct,
  output regDst,
  output aluSrc,
  output memtoReg,
  output regWrite,
  output memoWrite,
  output branch,
  output ExtOP,
  output [2:0] ALUctr
);

  wire andi_out, ori_out;
  wire [1:0] or_2_out;
  wire [2:0] bit_extender_1_out;

  and R_type (regDst, ~opcode[3], ~opcode[2], ~opcode[1], ~opcode[0]);  // AND_Gate
  and andi (andi_out, ~opcode[3], ~opcode[2], ~opcode[1], opcode[0]);  // AND_Gate
  Bit_Extender #(.in_width(4), .out_width(3)) bit_extender_1 (.in(funct), .out(bit_extender_1_out));
  and ori (ori_out, ~opcode[3], ~opcode[2], opcode[1], ~opcode[0]);  // AND_Gate
  and bnq (branch, ~opcode[3], ~opcode[2], opcode[1], opcode[0]);  // AND_Gate
  or or_1 (or_2_out[1], regDst, branch, memtoReg, memoWrite);
  or or_2 (or_2_out[0], ori_out, branch);
  and lw (memtoReg, ~opcode[3], opcode[2], ~opcode[1], ~opcode[0]);  // AND_Gate
  and sw (memoWrite, ~opcode[3], opcode[2], ~opcode[1], opcode[0]);  // AND_Gate
  or or_3 (aluSrc, andi_out, ori_out, memtoReg, memoWrite);
  or or_4 (regWrite, regDst, andi_out, ori_out, memtoReg);
  or or_5 (ExtOP, branch, memoWrite, memtoReg, andi_out);
  Multiplexer #(.width(3), .enable("false")) multiplexer_1 (
    .in0({regDst, or_2_out}), .in1(bit_extender_1_out), .out(ALUctr), .sel(regDst));
endmodule

module ALU (
  input  [15:0] in_1,
  input  [15:0] in_2,
  input  [2:0] in_3,
  output [15:0] out_4
);

  wire [15:0] adder_1_out, and_1_out, divider_1_out, multiplier_1_out, or_1_out, subtractor_1_out;

  assign and_1_out = in_1 & in_2;  // AND_Gate and_1, 16 bits wide
  assign or_1_out = in_1 | in_2;  // OR_Gate or_1, 16 bits wide
  Adder #(.width(16)) adder_1 (.a(in_1), .b(in_2), .out(adder_1_out));  // open: cin, cout
  Subtractor #(.width(16)) subtractor_1 (.a(in_1), .b(in_2), .out(subtractor_1_out));  // open: bin, bout
  Multiplier #(.width(16)) multiplier_1 (.a(in_1), .b(in_2), .out(multiplier_1_out));  // open: cin, cout
  Divider #(.width(16)) divider_1 (.a(in_1), .b(in_2), .out(divider_1_out));  // open: upper, rem
  Multiplexer #(.select(3), .width(16), .enable("false")) multiplexer_1 (
    .in0(and_1_out), .in1(or_1_out), .in2(adder_1_out), .in3(subtractor_1_out), .in4(multiplier_1_out),
    .in5(divider_1_out), .in6({16{1'b0}}), .in7({16{1'b0}}), .out(out_4), .sel(in_3));
endmodule

module CPU (
  input  in_1
);

  wire and_1_out, clock_1_out, comparator_1_eq, controlunit_1_alusrc, controlunit_1_branch,
       controlunit_1_extop, controlunit_1_memowrite, controlunit_1_memtoreg, controlunit_1_regdst,
       controlunit_1_regwrite, not_1_out;
  wire [2:0] controlunit_1_aluctr;
  wire [3:0] multiplexer_1_out, rom_1_data_3;
  wire [7:0] rom_1_data;
  wire [15:0] adder_1_out, adder_2_out, alu_1_out_4, bit_extender_1_out, multiplexer_2_out,
       multiplexer_3_out, multiplexer_4_out, pc_q, ram_1_data, registerfile_1_data1, registerfile_1_data2,
       shifter_1_out;
  wire [15:8] rom_1_data_2;

  Clock clock_1 (.out(clock_1_out));
  Register #(.width(16)) pc (.D(multiplexer_2_out), .Q(pc_q), .clk(clock_1_out), .clr(in_1));  // open: en
  ControlUnit controlunit_1 (
    .opcode(rom_1_data_3), .regDst(controlunit_1_regdst), .aluSrc(controlunit_1_alusrc),
    .memtoReg(controlunit_1_memtoreg), .regWrite(controlunit_1_regwrite),
    .memoWrite(controlunit_1_memowrite), .branch(controlunit_1_branch), .ExtOP(controlunit_1_extop),
    .funct(rom_1_data[3:0]), .ALUctr(controlunit_1_aluctr));
  Adder #(.width(16)) adder_1 (.a(16'h1), .b(pc_q), .out(adder_1_out));  // open: cin, cout
  ROM #(.addrWidth(16), .dataWidth(20)) rom_1 (
    .addr(pc_q), .data({rom_1_data_3, rom_1_data_2, rom_1_data}));  // open: sel
  assign bit_extender_1_out = {{8{controlunit_1_extop}}, rom_1_data};  // Bit_Extender bit_extender_1
  Multiplexer #(.width(4), .enable("false")) multiplexer_1 (
    .in0(rom_1_data_2[11:8]), .in1(rom_1_data[7:4]), .out(multiplexer_1_out), .sel(controlunit_1_regdst));
  RegisterFile registerfile_1 (
    .rd(multiplexer_1_out), .WreiteData(multiplexer_4_out), .rs(rom_1_data_2[15:12]),
    .data1(registerfile_1_data1), .rt(rom_1_data_2[11:8]), .data2(registerfile_1_data2),
    .RegWrite(controlunit_1_regwrite));
  Shifter #(.width(16)) shifter_1 (.in(bit_extender_1_out), .\dist (4'b0010), .out(shifter_1_out));
  Comparator #(.width(16)) comparator_1 (.a({16{1'b0}}), .b(alu_1_out_4), .eq(comparator_1_eq));  // open: gt, lt
  Adder #(.width(16)) adder_2 (.a(adder_1_out), .b(shifter_1_out), .out(adder_2_out));  // open: cin, cout
  not not_1 (not_1_out, comparator_1_eq);
  Multiplexer #(.width(16), .enable("false")) multiplexer_2 (
    .in0(adder_1_out), .in1(adder_2_out), .out(multiplexer_2_out), .sel(and_1_out));
  and and_1 (and_1_out, controlunit_1_branch, not_1_out);
  Multiplexer #(.width(16), .enable("false")) multiplexer_3 (
    .in0(registerfile_1_data2), .in1(bit_extender_1_out), .out(multiplexer_3_out), .sel(controlunit_1_alusrc));
  ALU alu_1 (.in_1(registerfile_1_data1), .in_2(multiplexer_3_out), .in_3(controlunit_1_aluctr), .out_4(alu_1_out_4));
  RAM #(.addrWidth(16), .dataWidth(16), .bus("separate")) ram_1 (
    .addr(alu_1_out_4), .din(registerfile_1_data2), .data(ram_1_data), .str(controlunit_1_memowrite),
    .clk(clock_1_out));  // open: sel, ld, clr
  Multiplexer #(.width(16), .enable("false")) multiplexer_4 (
    .in0(alu_1_out_4), .in1(ram_1_data), .out(multiplexer_4_out), .sel(controlunit_1_memtoreg));

  // Notes on the sheet:
  //   Instructions
  //   contents of rom_1 (hex, n*v repeats v):
  //   2110a 22204 1232 1243 1254 1265 1270 1281 50180 40900 33314 3341e
  //   memory
endmodule
